# Fritzing sketch Clase 10 Sensor PIR HC-SR501 (saved by Fritzing 0.9.10b)
breadboards: 1

parts:
  PIR1 = PIR sensor
  Mod1 = Raspberry Pi Pico
  LED1 = LED - 5mm [color="Blue (525nm)" current=0.030 package="5 mm [THT]"]

nets:
  N1: PIR1.VDD, Mod1.pin_40
  N2: PIR1.SIG, Mod1.pin_1
  N3: PIR1.GND, Mod1.pin_3, Mod1.pin_8, Mod1.pin_13, Mod1.pin_18, Mod1.pin_23, Mod1.pin_28, Mod1.pin_33, Mod1.pin_38, Mod1.pin_42, LED1.cathode
  N4: Mod1.pin_7, LED1.anode

notes:
  Pines:
  PIR = GPIO 1
  LED = GPIO 4

custom parts:
  Raspberry Pi Pico: Raspberry Pi Pico. Based around the RP2040 microcontroller the Pico is a low cost microcontroller device bringing Raspberry Pi quality, cost, and easy of use to the microcontroller space. Jan 2021, Split part in to two versions: tht (this one) and SMD. This one will drill holes for a .1 in header in pcb to allow plugging in the module as well as providing pads to solder the module to the top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
