# Fritzing sketch Clase 4 (Pulsador) (saved by Fritzing 0.9.3b)
breadboards: 1

parts:
  Mod1 = Raspberry Pi Pico
  S2 = Pushbutton [package="[THT]"]
  R1 = Resistor [tolerance=±5% resistance=10k package=THT]
  LED1 = LED - 5mm [color="Red (633nm)" package="5 mm [THT]"]
  LED2 = LED - 5mm [color="Blue (430nm)" package="5 mm [THT]"]
  R2 = Resistor [tolerance=±5% resistance=150 package=THT]
  R3 = Resistor [tolerance=±5% resistance=150 package=THT]
  S1 = Pushbutton [package="[THT]"]

nets:
  N1: Mod1.pin_3, Mod1.pin_8, Mod1.pin_13, Mod1.pin_18, Mod1.pin_23, Mod1.pin_28, Mod1.pin_33, Mod1.pin_38, R1.Pin_1, R2.Pin_0, R3.Pin_0
  N2: Mod1.pin_19, LED2.anode
  N3: Mod1.pin_20, LED1.anode
  N4: Mod1.pin_21, S1.Pin_3, S1.Pin_4
  N5: Mod1.pin_22, S2.Pin_1, S2.Pin_2, R1.Pin_0
  N6: Mod1.pin_36, S2.Pin_3, S2.Pin_4, S1.Pin_1, S1.Pin_2
  N7: LED1.cathode, R2.Pin_1
  N8: LED2.cathode, R3.Pin_1

custom parts:
  Raspberry Pi Pico: Raspberry Pi Pico. Based around the RP2040 microcontroller the Pico is a low cost microcontroller device bringing Raspberry Pi quality, cost, and easy of use to the microcontroller space. Jan 2021, Split part in to two versions: tht (this one) and SMD. This one will drill holes for a .1 in header in pcb to allow plugging in the module as well as providing pads to solder the module to the top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
