# Fritzing sketch Clase 7 (Bluetooth-Receptor) (saved by Fritzing 0.9.3b)
breadboards: 1

parts:
  Mod1 = Raspberry Pi Pico
  LED1 = LED - 5mm [color="Red (633nm)" package="5 mm [THT]"]
  LED2 = LED - 5mm [color="Yellow (595nm)" package="5 mm [THT]"]
  LED3 = LED - 5mm [color="Green (555nm)" package="5 mm [THT]"]
  LED4 = LED - 5mm [color="Blue (430nm)" package="5 mm [THT]"]
  Componente1 = HC-05 [part_number=HC-05 package="breakout board"]
  R1 = Resistor [tolerance=±5% resistance=150 package=THT]
  R2 = Resistor [tolerance=±5% resistance=150 package=THT]
  R3 = Resistor [tolerance=±5% resistance=150 package=THT]
  R4 = Resistor [tolerance=±5% resistance=150 package=THT]

nets:
  N1: Mod1.pin_1, Componente1.RXD
  N2: Mod1.pin_2, Componente1.TXD
  N3: Mod1.pin_3, Mod1.pin_8, Mod1.pin_13, Mod1.pin_18, Mod1.pin_23, Mod1.pin_28, Mod1.pin_33, Mod1.pin_38, Mod1.pin_42, LED1.cathode, LED2.cathode, LED3.cathode, LED4.cathode, Componente1.GND
  N4: Mod1.pin_4, R1.Pin_0
  N5: Mod1.pin_6, R4.Pin_0
  N6: Mod1.pin_15, R3.Pin_0
  N7: Mod1.pin_20, R2.Pin_0
  N8: Mod1.pin_39, Componente1.VCC
  N9: LED1.anode, R1.Pin_1
  N10: LED2.anode, R4.Pin_1
  N11: LED3.anode, R3.Pin_1
  N12: LED4.anode, R2.Pin_1

notes:
  TX CON RX y viceversa

custom parts:
  Raspberry Pi Pico: Raspberry Pi Pico. Based around the RP2040 microcontroller the Pico is a low cost microcontroller device bringing Raspberry Pi quality, cost, and easy of use to the microcontroller space. Jan 2021, Split part in to two versions: tht (this one) and SMD. This one will drill holes for a .1 in header in pcb to allow plugging in the module as well as providing pads to solder the module to the top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
  HC-05: A commonly available HC-05 Bluetooth breakout board.
